# Fritzing sketch Arduino_Controller_Schematics (saved by Fritzing 0.9.3b)
breadboards: 1

parts:
  Part1 = Arduino Nano (Rev3.0) (ICSP)
  BUTTON1 = Pushbutton [package="[SMD]"]
  BUTTON2 = Pushbutton [package="[SMD]"]
  R1 = Resistor [tolerance=±5% resistance=10k package="0603 [SMD]"]
  R2 = Resistor [tolerance=±5% resistance=10k package="0603 [SMD]"]
  LED1 = smd LED [color="Red (633nm)" package="0805 [SMD]"]
  S1 = SPST Switch [package=switch-spst-smd-a]
  NORMALDE_BUNUN_LED_RING_OLMASI_GEREKIYOR_AMA_BU_PROGRAMDA_BULAMADIM_BUNUN_DETAYLARI_README_MD'DE = RGB LED - (4 legs) [package="5 mm [THT]"]
  R3 = Rotary Potentiometer (Small) [maximum_resistance=100kΩ package=THT]

nets:
  N1: Part1.GND, R1.Pin_1, R2.Pin_1, LED1.cathode, S1.O, R3.leg1
  N2: Part1.D2, BUTTON2.Pin_3, BUTTON2.Pin_4
  N3: Part1.D5, NORMALDE_BUNUN_LED_RING_OLMASI_GEREKIYOR_AMA_BU_PROGRAMDA_BULAMADIM_BUNUN_DETAYLARI_README_MD'DE.blue_cathode
  N4: Part1.D6, NORMALDE_BUNUN_LED_RING_OLMASI_GEREKIYOR_AMA_BU_PROGRAMDA_BULAMADIM_BUNUN_DETAYLARI_README_MD'DE.green_cathode
  N5: Part1.D7, Part1.5V, BUTTON1.Pin_3, BUTTON1.Pin_4, S1.S, NORMALDE_BUNUN_LED_RING_OLMASI_GEREKIYOR_AMA_BU_PROGRAMDA_BULAMADIM_BUNUN_DETAYLARI_README_MD'DE.common_anode, R3.leg2
  N6: Part1.D10, NORMALDE_BUNUN_LED_RING_OLMASI_GEREKIYOR_AMA_BU_PROGRAMDA_BULAMADIM_BUNUN_DETAYLARI_README_MD'DE.red_cathode
  N7: Part1.A2, R3.wiper
  N8: Part1.A1, S1.P
  N9: Part1.D11/MOSI, LED1.anode
  N10: BUTTON1.Pin_1, BUTTON1.Pin_2, BUTTON2.Pin_1, BUTTON2.Pin_2, R1.Pin_0, R2.Pin_0
